// Logisim project 2105061.circ as structural Verilog: 1 circuit, main circuit main
module main (
  input  CONST_1,
  input  X_0,
  input  in_3,
  input  CONST_1_2,
  input  X_1,
  output out_6,
  output out_7
);

  wire main_1_s1;

  _2105061_main main_1 (.x2(CONST_1), .x3(X_0), .x4(in_3), .s1(main_1_s1), .s2(out_6));  // open: x1, a1, a2, s3, s4
  _2105061_main main_2 (.x2(CONST_1_2), .x3(X_1), .x4(main_1_s1), .s2(out_7));  // open: x1, a1, a2, s1, s3, s4
endmodule
