// Logisim project 2105061.circ as structural Verilog: 1 circuit, main circuit main
module main (
  input  x1,
  input  x2,
  input  x3,
  input  x4,
  input  a1,
  input  a2,
  output s1,
  output s2,
  output s3,
  output s4
);

  wire xor_1_out, xor_2_out, xor_3_out, xor_4_out;

  xor xor_1 (xor_1_out, x1, a2);
  xor xor_2 (xor_2_out, x2, a2);
  xor xor_3 (xor_3_out, x3, a2);
  xor xor_4 (xor_4_out, x4, a2);
  // _7483 7483_1: pin names not known; wires that end beside it: xor_2_out, s1, 1'b0, xor_1_out, s2, a1, 1'b1, 1'b0, 1'b0, 1'b0, xor_3_out, s3, s4, xor_4_out, 1'b0
endmodule
